# Fritzing sketch diagram (saved by Fritzing 0.8.7b)
breadboards: 1

parts:
  Part1 = Arduino Uno (Rev3)
  U1 = microSD Socket [package=micro-sd-socket-pp]
  S1 = Pushbutton [package="[THT]"]
  S2 = Pushbutton [package="[THT]"]
  SP1 = SPEAKER [package=pcb_mount_speaker]
  R1 = Resistor [package="2512 [SMD]"]
  R2 = Trimmer Potentiometer [maximum_resistance=10kΩ package=THT]  # not connected
  U2 = LM386 [package=dip08]
  C1 = Capacitor Polarized [package=cpol-radial-10uf-25v]
  C2 = Capacitor Polarized [package=panasonic_c]
  R3 = Resistor [package="2512 [SMD]"]
  C3 = Capacitor Polarized [package=cpol-radial-10uf-25v]
  C4 = Capacitor Polarized [package=panasonic_c]

nets:
  N1: Part1.D9_PWM, R1.Pin_0
  N2: Part1.D11_PWM/MOSI, U1.CS
  N3: Part1.D12/MISO, Part1.D13/SCK, Part1.5V, U1.SHIELD, SP1.-, U2.V+, C2.-
  N4: Part1.D1/TX, S1.Pin_3, S1.Pin_4
  N5: Part1.D2, S2.Pin_3, S2.Pin_4
  N6: Part1.D4, U1.DI
  N7: Part1.GND, U1.NC, S1.Pin_1, S1.Pin_2, S2.Pin_1, S2.Pin_2, SP1.+, U2.-IN, U2.V-, C3.+, C4.-
  N8: U2.GAIN, C1.+, C1.-
  N9: U2.OUT, C2.+, R3.Pin_0
  N10: R3.Pin_1, C3.-
